# Fritzing sketch circut (saved by Fritzing 0.9.6b)
breadboards: 1

parts:
  Part2 = Bluetooth HC-05 Macho
  R1 = Resistor [tolerance=±1% power=0.25 resistance=2000 package=THT]
  R2 = Resistor [tolerance=±1% power=0.25 resistance=1000 package=THT]
  Part1 = Arduino Uno (Rev3)
  R3 = Resistor [tolerance=±1% power=0.25 resistance=220 package=THT]
  LED1 = LED - 5mm [color="Red (633nm)" current=0.030 package="5 mm [THT]"]

nets:
  N1: Part2.TXD, Part1.D0/RX
  N2: Part2.RXD, R1.Pin_1, R2.Pin_1
  VCC: Part2.VCC, Part1.5V
  GND: Part2.GND, R1.Pin_0, Part1.GND, R3.Pin_0
  N3: R2.Pin_0, Part1.D1/TX
  N4: Part1.D13/SCK, LED1.anode
  N5: R3.Pin_1, LED1.cathode

// code stored in the sketch: Untitled.ino
#define led_pin 13


void setup() {
    pinMode(led_pin, OUTPUT);
    Serial.begin(9600);
}


void loop() {
   if(Serial.available() > 0){
    char recieved = Serial.read();
    if(recieved == 'H'){
        digitalWrite(led_pin, HIGH);
    Serial.print("On;");
    }else if(recieved == 'L'){
        digitalWrite(led_pin, LOW);
        Serial.print("Off;");
    }else{
        Serial.print("Error, Unknown command;");
    }
  }
}
